// Logisim project 8by6multiplexer.circ as structural Verilog: 1 circuit, main circuit main
module main (
  input  [5:0] in_1,
  input  [5:0] in_2,
  input  [5:0] in_3,
  input  [5:0] in_4,
  input  [5:0] in_5,
  input  [5:0] in_6,
  input  [5:0] in_7,
  input  [5:0] in_8,
  input  [2:0] Select__you_need_to_change_the_Data_Bits_of_this_pin,
  output [5:0] Out
);

  wire [5:0] multiplexer_1_out, multiplexer_2_out, multiplexer_3_out, multiplexer_4_out, multiplexer_5_out,
       multiplexer_7_out;

  Multiplexer #(.width(6), .enable("false")) multiplexer_1 (
    .in0(in_1), .in1(in_2), .out(multiplexer_1_out),
    .sel(Select__you_need_to_change_the_Data_Bits_of_this_pin[0]));
  Multiplexer #(.width(6), .enable("false")) multiplexer_2 (
    .in0(in_3), .in1(in_4), .out(multiplexer_2_out),
    .sel(Select__you_need_to_change_the_Data_Bits_of_this_pin[0]));
  Multiplexer #(.width(6), .enable("false")) multiplexer_3 (
    .in0(in_5), .in1(in_6), .out(multiplexer_3_out),
    .sel(Select__you_need_to_change_the_Data_Bits_of_this_pin[0]));
  Multiplexer #(.width(6), .enable("false")) multiplexer_4 (
    .in0(in_7), .in1(in_8), .out(multiplexer_4_out),
    .sel(Select__you_need_to_change_the_Data_Bits_of_this_pin[0]));
  Multiplexer #(.width(6), .enable("false")) multiplexer_5 (
    .in0(multiplexer_1_out), .in1(multiplexer_2_out), .out(multiplexer_5_out),
    .sel(Select__you_need_to_change_the_Data_Bits_of_this_pin[1]));
  Multiplexer #(.width(6), .enable("false")) multiplexer_6 (
    .in0(multiplexer_5_out), .in1(multiplexer_7_out), .out(Out),
    .sel(Select__you_need_to_change_the_Data_Bits_of_this_pin[2]));
  Multiplexer #(.width(6), .enable("false")) multiplexer_7 (
    .in0(multiplexer_3_out), .in1(multiplexer_4_out), .out(multiplexer_7_out),
    .sel(Select__you_need_to_change_the_Data_Bits_of_this_pin[1]));
  Multiplexer #(.width(6), .enable("false")) multiplexer_8 ();  // open: in0, in1, out, sel

  // Notes on the sheet:
  //   Example of a 2-input, 6-bit multiplexer; you'll need more of these
endmodule
