// Logisim project parity.circ as structural Verilog: 2 circuits, main circuit main
module main (
  input  [15:0] X,
  output [15:0] result
);

  wire [15:0] subcircuit_1_out_3, subcircuit_2_out_3, subcircuit_3_out_3, subcircuit_4_out_3;

  subcircuit subcircuit_1 (.y(X), .C(16'h1), .out_3(subcircuit_1_out_3));
  subcircuit subcircuit_2 (.y(subcircuit_1_out_3), .C(16'h2), .out_3(subcircuit_2_out_3));
  subcircuit subcircuit_3 (.y(subcircuit_2_out_3), .C(16'h4), .out_3(subcircuit_3_out_3));
  subcircuit subcircuit_4 (.y(subcircuit_3_out_3), .C(16'h8), .out_3(subcircuit_4_out_3));
  assign result = subcircuit_4_out_3 & 16'h1;  // AND_Gate and_1, 16 bits wide
endmodule

module subcircuit (
  input  [15:0] y,
  input  [15:0] C,
  output [15:0] out_3
);

  wire [15:0] shifter_1_out;

  Shifter #(.width(16), .shift("lr")) shifter_1 (.in(y), .\dist (C[3:0]), .out(shifter_1_out));
  assign out_3 = y ^ shifter_1_out;  // XOR_Gate xor_1, 16 bits wide
endmodule
