// Logisim project lab-accum.circ as structural Verilog: 1 circuit, main circuit main
module main (
  input  Reset,
  input  [7:0] in_2,
  output [7:0] accumulator
);

  wire clock_1_out;
  wire [7:0] adder_1_out, multiplexer_1_out;

  Adder adder_1 (.a(in_2), .b(accumulator), .out(adder_1_out));  // open: cin, cout
  Multiplexer #(.width(8), .enable("false")) multiplexer_1 (
    .in0(adder_1_out), .in1({8{1'b0}}), .out(multiplexer_1_out), .sel(Reset));
  Clock clock_1 (.out(clock_1_out));
  Register register_1 (.D(multiplexer_1_out), .Q(accumulator), .clk(clock_1_out));  // open: en, clr
endmodule
