// Logisim project lab4-test.circ as structural Verilog: 1 circuit, main circuit main
module main (
  output Z,
  output out_2
);

  wire clock_1_out, d_ff_1_q, d_ff_2_q, rom_1_data, rom_2_data;
  wire [2:0] counter_1_q, counter_2_q;

  Counter #(.width(3), .max('h7), .ongoal("stay")) counter_1 (
    .Q(counter_1_q), .clk(clock_1_out));  // open: load, D, count, carry, clr
  Counter #(.width(3), .max('h7)) counter_2 (.Q(counter_2_q), .clk(clock_1_out));  // open: load, D, count, carry, clr
  Clock clock_1 (.out(clock_1_out));
  ROM #(.addrWidth(3), .dataWidth(1)) rom_1 (.addr(counter_1_q), .data(rom_1_data));  // open: sel
  ROM #(.addrWidth(3), .dataWidth(1)) rom_2 (.addr(counter_2_q), .data(rom_2_data));  // open: sel
  D_Flip_Flop d_ff_1 (.clk(clock_1_out), .D(rom_1_data), .Q(d_ff_1_q));  // open: Qn, preset, en, reset
  D_Flip_Flop d_ff_2 (.clk(clock_1_out), .D(d_ff_1_q), .Q(d_ff_2_q));  // open: Qn, preset, en, reset
  and and_1 (Z, d_ff_1_q, d_ff_2_q);
  Comparator #(.width(1)) comparator_1 (.a(Z), .b(rom_2_data), .eq(out_2));  // open: gt, lt

  // Notes on the sheet:
  //   contents of rom_1 (hex, n*v repeats v):
  //   0 1 0 1 1 1
  //   contents of rom_2 (hex, n*v repeats v):
  //   5*0 1 1
endmodule
