// Logisim project lab-mem-romtt.circ as structural Verilog: 1 circuit, main circuit main
module main (
  input  In0,
  input  In1,
  input  In2,
  output [3:0] Out
);

  ROM #(.addrWidth(3), .dataWidth(4)) rom_1 (.addr({In2, In1, In0}), .data(Out));  // open: sel

  // Notes on the sheet:
  //   DO NOT MOVE OR RENAME THE GIVEN PINS!
  //   contents of rom_1 (hex, n*v repeats v):
  //   0 1 4 8 3 6 c 7
endmodule
