// Logisim project lab-cl-errors.circ as structural Verilog: 1 circuit, main circuit main
module main (
  input  in_1,
  input  in_2
);

  wire undriven;

  not not_1 (in_1, in_2);
  // AND_Gate and_1 has open pins: in1=in_1, in3=undriven, in4=in_1, out=open
endmodule
