// Logisim project lab-cl-mux.circ as structural Verilog: 1 circuit, main circuit main
module main (
  input  In0,
  input  In1,
  input  Select,
  output Out,
  output out_5,
  output out_6
);

  wire and_1_out, and_2_out, and_3_out, xor_1_out;

  Multiplexer #(.enable("false")) multiplexer_1 (.in0(In0), .in1(In1), .out(Out), .sel(Select));
  and and_1 (and_1_out, In0, In1);
  xor xor_1 (xor_1_out, In0, Select);
  and and_2 (and_2_out, In1, Select);
  and and_3 (and_3_out, In0, xor_1_out);
  Comparator #(.width(1)) comparator_1 (.a(Out), .b(out_6), .eq(out_5));  // open: gt, lt
  or or_1 (out_6, and_3_out, and_1_out, and_2_out);
endmodule
