// Logisim project testing_example.circ as structural Verilog: 1 circuit, main circuit main
module main (
  input  a,
  input  b,
  output matched
);

  wire and_1_out, and_2_out, not_1_out, not_2_out, or_1_out, xnor_1_out;

  not not_1 (not_1_out, a);
  not not_2 (not_2_out, b);
  and and_1 (and_1_out, a, b);
  and and_2 (and_2_out, not_1_out, not_2_out);
  xnor xnor_1 (xnor_1_out, a, b);
  or or_1 (or_1_out, and_1_out, and_2_out);
  Comparator #(.width(1)) comparator_1 (.a(or_1_out), .b(xnor_1_out), .eq(matched));  // open: gt, lt

  // Notes on the sheet:
  //   try all 4 inputs
  //   Implementation
  //   Black box
  //   should be 1 for all inputs
endmodule
