// Logisim project arithmetic-problem.circ as structural Verilog: 1 circuit, main circuit main
module main (
  input  [5:0] A,
  input  [5:0] B,
  input  [5:0] C,
  input  [2:0] _3,
  output [5:0] out_5
);

  wire [5:0] adder_1_out, negator_1_out, shifter_1_out;

  Negator #(.width(6)) negator_1 (.in(A), .out(negator_1_out));
  Shifter #(.width(6)) shifter_1 (.in(C), .\dist (_3), .out(shifter_1_out));
  Adder #(.width(6)) adder_1 (.a(negator_1_out), .b(B), .out(adder_1_out));  // open: cin, cout
  Subtractor #(.width(6)) subtractor_1 (.a(adder_1_out), .b(shifter_1_out), .out(out_5));  // open: bin, bout
endmodule
