// Logisim project multiplexer-problem.circ as structural Verilog: 1 circuit, main circuit main
module main (
  input  [5:0] InA,
  input  [5:0] InB,
  input  [5:0] InC,
  input  [5:0] InD,
  input  [1:0] Select,
  output [5:0] Output
);

  Multiplexer #(.select(2), .width(6), .enable("false")) multiplexer_1 (
    .in0(InA), .in1(InB), .in2(InC), .in3(InD), .out(Output), .sel(Select));
endmodule
