// Logisim project prelab 11.circ as structural Verilog: 1 circuit, main circuit main
module main (
  input  [7:0] in_1,
  output [7:0] out_2
);

  wire clock_1_out;
  wire [7:0] adder_1_out;

  Adder adder_1 (.a(in_1), .b(out_2), .out(adder_1_out));  // open: cin, cout
  Clock clock_1 (.out(clock_1_out));
  Register register_1 (.D(adder_1_out), .Q(out_2), .clk(clock_1_out));  // open: en, clr
endmodule
